# Fritzing sketch TinyRover (saved by Fritzing 0.7.12b)
breadboards: 1

parts:
  ATtiny85 = attiny85 [package=dip]
  L293D = L293D [package=THT]
  M1 = DC Motor
  M2 = DC Motor
  J1 = Infrared Proximity Sensor [part_number=GP2Y0A21YK0F]
  U1 = Voltage Regulator - 5V [part_number=L78S05CV package="TO220 [THT]"]
  JACK1 = 2.1mm Barrel Jack with Terminal Block

nets:
  N1: ATtiny85.Pin_2, L293D.In_2
  N2: ATtiny85.Pin_3, L293D.In_1
  GND: ATtiny85.Pin_4, L293D.0V, J1.GND, U1.GND, JACK1.NEG
  N3: ATtiny85.Pin_5, L293D.In_4
  N4: ATtiny85.Pin_6, L293D.In_3
  N5: ATtiny85.Pin_7, J1.Vout
  N6: ATtiny85.Pin_8, L293D.Enable_1, L293D.+Vmotor, L293D.Enable_2, L293D.+V, J1.Vcc, U1.output_voltage
  N7: L293D.Out_1_(_Controlled_by_Enable_1_), M2.pin_2
  N8: L293D.Out_2_(_Controlled_by_Enable_1_), M2.pin_1
  N9: L293D.Out_3_(_Controlled_by_Enable_2_), M1.pin_2
  N10: L293D.Out_4_(_Controlled_by_Enable_2_), M1.pin_1
  N11: U1.input_voltage, JACK1.POS
